# Fritzing sketch old___circuit_anxious (saved by Fritzing 0.9.2b)
circuit board: 2.8875cm x 2.16663cm
breadboards: 1

parts:
  ATTINY84 = IC, DIP package, 14 pins [chip_label=ATTINY84]
  R1 = Resistor [tolerance=±5% resistance=10k package=THT]
  D1 = Rectifier Diode [part_number=1N4001 package="300 mil [THT]"]
  Q1 = Basic FET N-Channel [package="TO220 [THT]"]
  MOTOR = DC Motor [part_number=Motor]
  SERVO = Basic Servo
  POWER = Battery block 9V
  SONAR = female pin header, 3 pins [form="♀ (female)"]

nets:
  N1: ATTINY84.pin1, D1.cathode, MOTOR.pin_1, SERVO.vcc, POWER.+, SONAR.pin2
  N2: ATTINY84.pin5, SERVO.pulse
  N3: ATTINY84.pin6, SONAR.pin1
  N4: ATTINY84.pin8, R1.Pin_0, Q1.gate
  N5: ATTINY84.pin14, R1.Pin_1, Q1.source, SERVO.gnd, POWER.-, SONAR.pin3
  N6: D1.anode, Q1.drain, MOTOR.pin_2
